// Logisim project Project.circ as structural Verilog: 14 circuits, main circuit main
module main (
);

  wire cu_1_address, cu_1_ramwrite, fetch_1_gp_x, fetch_1_gp_y, ir_1_argv_0, not_1_out, store_1_ram_write;
  wire [1:0] cu_1_alu_op, fetch_1_write_2;
  wire [2:0] ir_1_opcode;
  wire [3:0] ir_1_argv_1, ir_1_instrcacheaddr;
  wire [7:0] alu_1_alu_out, cache_1_out_5, demultiplexer_1_out0, demultiplexer_1_out1, fetch_1_val,
       fetch_1_x_2, fetch_1_y_2, gpregisters_1_read0, gpregisters_1_read1, multiplexer_1_out, store_1_value_2;

  CU cu_1 (.in_1(ir_1_opcode), .ALU_OP(cu_1_alu_op), .address(cu_1_address), .ramwrite(cu_1_ramwrite));  // open: out_2
  IR ir_1 (
    .in_1(4'b0000), .OPCODE(ir_1_opcode), .argv_0(ir_1_argv_0), .argv_1(ir_1_argv_1),
    .instrcacheaddr(ir_1_instrcacheaddr), .instrval(cache_1_out_5));
  cache cache_1 (.raddress(ir_1_instrcacheaddr), .status(1'b0), .out_5(cache_1_out_5));  // open: waddress, writeval
  fetch fetch_1 (
    .register_x(ir_1_argv_0), .address_2(ir_1_argv_1), .X_2(fetch_1_x_2), .Y_2(fetch_1_y_2),
    .X(gpregisters_1_read0), .Y(gpregisters_1_read1), .GP_x(fetch_1_gp_x), .GP_y(fetch_1_gp_y),
    .writeval(store_1_value_2), .val(fetch_1_val), .write_2(fetch_1_write_2), .address(cu_1_address));  // open: write
  gpregisters gpregisters_1 (
    .select0(fetch_1_gp_x), .select1(fetch_1_gp_y), .read0(gpregisters_1_read0), .read1(gpregisters_1_read1),
    .writeval(fetch_1_val), .write(fetch_1_write_2));
  ALU alu_1 (.ALU_OUT(alu_1_alu_out), .in_2(fetch_1_x_2), .in_3(fetch_1_y_2), .in_1(cu_1_alu_op));  // open: Status
  not not_1 (not_1_out, cu_1_address);
  Demultiplexer #(.width(8)) demultiplexer_1 (
    .out0(demultiplexer_1_out0), .out1(demultiplexer_1_out1), .in(alu_1_alu_out), .sel(cu_1_address));  // open: en
  Multiplexer #(.width(8), .enable("false")) multiplexer_1 (
    .in0(fetch_1_x_2), .in1(demultiplexer_1_out0), .out(multiplexer_1_out), .sel(not_1_out));
  store store_1 (
    .value(multiplexer_1_out), .cache_address(demultiplexer_1_out1), .ramwrite(cu_1_ramwrite),
    .value_2(store_1_value_2), .ram_write(store_1_ram_write));  // open: register_address, cache_address_2, register_write
  cache cache_2 (.status(store_1_ram_write));  // open: raddress, waddress, writeval, out_5
endmodule

module Half_Adder (
  input  in_1,
  input  in_2,
  output out_3,
  output out_4
);

  wire not_1_out, or_1_out;

  or or_1 (or_1_out, in_1, in_2);
  and and_1 (out_4, in_1, in_2);
  and and_2 (out_3, or_1_out, not_1_out);
  not not_1 (not_1_out, out_4);
endmodule

module Full_Adder (
  input  in_1,
  input  in_2,
  input  in_3,
  output out_4,
  output out_5
);

  wire half_adder_1_out_3, half_adder_1_out_4, half_adder_2_out_4;

  Half_Adder half_adder_1 (.in_1(in_1), .in_2(in_2), .out_3(half_adder_1_out_3), .out_4(half_adder_1_out_4));
  Half_Adder half_adder_2 (.in_1(half_adder_1_out_3), .in_2(in_3), .out_3(out_4), .out_4(half_adder_2_out_4));
  or or_1 (out_5, half_adder_2_out_4, half_adder_1_out_4);
endmodule

module Addition (
  input  [7:0] ALU_Left,
  input  [7:0] ALU_Right,
  output [7:0] out_3,
  output Overflow
);

  wire full_adder_1_out_5, full_adder_2_out_5, full_adder_3_out_5, full_adder_4_out_5, full_adder_5_out_5,
       full_adder_6_out_5, half_adder_1_out_4;

  Half_Adder half_adder_1 (.in_1(ALU_Left[0]), .in_2(ALU_Right[0]), .out_3(out_3[0]), .out_4(half_adder_1_out_4));
  Full_Adder full_adder_1 (
    .in_1(half_adder_1_out_4), .in_2(ALU_Right[1]), .in_3(ALU_Left[1]), .out_4(out_3[1]),
    .out_5(full_adder_1_out_5));
  Full_Adder full_adder_2 (
    .in_1(full_adder_1_out_5), .in_2(ALU_Right[2]), .in_3(ALU_Left[2]), .out_4(out_3[2]),
    .out_5(full_adder_2_out_5));
  Full_Adder full_adder_3 (
    .in_1(full_adder_2_out_5), .in_2(ALU_Right[3]), .in_3(ALU_Left[3]), .out_4(out_3[3]),
    .out_5(full_adder_3_out_5));
  Full_Adder full_adder_4 (
    .in_1(full_adder_3_out_5), .in_2(ALU_Right[4]), .in_3(ALU_Left[4]), .out_4(out_3[4]),
    .out_5(full_adder_4_out_5));
  Full_Adder full_adder_5 (
    .in_1(full_adder_4_out_5), .in_2(ALU_Right[5]), .in_3(ALU_Left[5]), .out_4(out_3[5]),
    .out_5(full_adder_5_out_5));
  Full_Adder full_adder_6 (
    .in_1(full_adder_5_out_5), .in_2(ALU_Right[6]), .in_3(ALU_Left[6]), .out_4(out_3[6]),
    .out_5(full_adder_6_out_5));
  Full_Adder full_adder_7 (
    .in_1(full_adder_6_out_5), .in_2(ALU_Right[7]), .in_3(ALU_Left[7]), .out_4(out_3[7]), .out_5(Overflow));

  // Notes on the sheet:
  //   ALU-Out
endmodule

module _2_s_Complement (
  input  [7:0] in_1,
  output [7:0] out_2
);

  wire half_adder_1_out_4, half_adder_2_out_4, half_adder_3_out_4, half_adder_4_out_4, half_adder_5_out_4,
       half_adder_6_out_4, half_adder_7_out_4, not_1_out, not_2_out, not_3_out, not_4_out, not_5_out,
       not_6_out, not_7_out, not_8_out, not_9_out, or_1_out;

  not not_1 (not_1_out, in_1[6]);
  not not_2 (not_2_out, in_1[7]);
  not not_3 (not_3_out, in_1[2]);
  not not_4 (not_4_out, in_1[4]);
  not not_5 (not_5_out, in_1[3]);
  not not_6 (not_6_out, in_1[5]);
  not not_7 (not_7_out, not_8_out);
  not not_8 (not_8_out, in_1[0]);
  not not_9 (not_9_out, in_1[1]);
  or or_1 (or_1_out, not_7_out, not_8_out);
  Half_Adder half_adder_1 (.in_1(or_1_out), .in_2(not_8_out), .out_3(out_2[0]), .out_4(half_adder_1_out_4));
  Half_Adder half_adder_2 (.in_1(half_adder_1_out_4), .in_2(not_9_out), .out_3(out_2[1]), .out_4(half_adder_2_out_4));
  Half_Adder half_adder_3 (.in_1(half_adder_2_out_4), .in_2(not_3_out), .out_3(out_2[2]), .out_4(half_adder_3_out_4));
  Half_Adder half_adder_4 (.in_1(half_adder_3_out_4), .in_2(not_5_out), .out_3(out_2[3]), .out_4(half_adder_4_out_4));
  Half_Adder half_adder_5 (.in_1(half_adder_4_out_4), .in_2(not_4_out), .out_3(out_2[4]), .out_4(half_adder_5_out_4));
  Half_Adder half_adder_6 (.in_1(half_adder_5_out_4), .in_2(not_6_out), .out_3(out_2[5]), .out_4(half_adder_6_out_4));
  Half_Adder half_adder_7 (.in_1(half_adder_6_out_4), .in_2(not_1_out), .out_3(out_2[6]), .out_4(half_adder_7_out_4));
  Half_Adder half_adder_8 (.in_1(half_adder_7_out_4), .in_2(not_2_out), .out_3(out_2[7]));  // open: out_4
endmodule

module ALU (
  input  [1:0] in_1,
  input  [7:0] in_2,
  input  [7:0] in_3,
  output [7:0] ALU_OUT,
  output [3:0] Status
);

  wire and_3_out;
  wire [1:0] and_4_out;
  wire [7:0] addition_1_out_3, multiplexer_1_out, n2_s_complement_1_out_2;

  and and_1 (and_4_out[1], ~in_1[0], ~in_1[1]);  // AND_Gate
  _2_s_Complement u_2_s_complement_1 (.in_1(in_3), .out_2(n2_s_complement_1_out_2));
  // AND_Gate and_2 has open pins: in0=in_1[0], in1=in_1[1], out=open
  and and_3 (and_3_out, in_1[0], ~in_1[1]);  // AND_Gate
  Addition addition_1 (.out_3(addition_1_out_3), .ALU_Left(multiplexer_1_out), .ALU_Right(in_2), .Overflow(Status[0]));
  Multiplexer #(.width(8)) multiplexer_1 (
    .in0(in_3), .in1(n2_s_complement_1_out_2), .out(multiplexer_1_out), .sel(and_3_out));  // open: en
  and and_4 (and_4_out[0], in_1[0], in_1[1]);
  // NOT_Gate not_1 is placed but not wired
  Multiplexer #(.select(2), .width(8)) multiplexer_2 (
    .in0(addition_1_out_3), .in1(n2_s_complement_1_out_2), .in2(in_3), .out(ALU_OUT), .sel(and_4_out));  // open: in3, en

  // Notes on the sheet:
  //   ALU-L
  //   ALU-R
  //   NOP
  //   ADD
  //   SUB
  //   MULT
  //   BRE0
  //   OPERATIONS
  //   00
  //   01
  //   10
  //   11
  //   COMP ( -)
  //   default state
  //   Bit 0 - Overflow
endmodule

module register (
  output [7:0] out_1,
  output [7:0] out_2
);

  wire not_1_out, not_2_out, not_3_out, not_4_out, not_5_out, not_6_out, not_7_out, not_8_out;

  not not_1 (not_1_out, out_1[0]);
  not not_2 (not_2_out, out_1[1]);
  not not_3 (not_3_out, out_1[2]);
  not not_4 (not_4_out, out_1[3]);
  not not_5 (not_5_out, out_1[4]);
  not not_6 (not_6_out, out_1[5]);
  not not_7 (not_7_out, out_1[6]);
  not not_8 (not_8_out, out_1[7]);
  S_R_Flip_Flop s_r_ff_1 (.S(out_1[0]), .R(not_1_out), .Q(out_2[0]));  // open: clk, Qn, preset, reset, en
  S_R_Flip_Flop s_r_ff_2 (.S(out_1[1]), .R(not_2_out), .Q(out_2[1]));  // open: clk, Qn, preset, reset, en
  S_R_Flip_Flop s_r_ff_3 (.S(out_1[2]), .R(not_3_out), .Q(out_2[2]));  // open: clk, Qn, preset, reset, en
  S_R_Flip_Flop s_r_ff_4 (.S(out_1[3]), .R(not_4_out), .Q(out_2[3]));  // open: clk, Qn, preset, reset, en
  S_R_Flip_Flop s_r_ff_5 (.S(out_1[4]), .R(not_5_out), .Q(out_2[4]));  // open: clk, Qn, preset, reset, en
  S_R_Flip_Flop s_r_ff_6 (.S(out_1[5]), .R(not_6_out), .Q(out_2[5]));  // open: clk, Qn, preset, reset, en
  S_R_Flip_Flop s_r_ff_7 (.S(out_1[6]), .R(not_7_out), .Q(out_2[6]));  // open: clk, Qn, preset, reset, en
  S_R_Flip_Flop s_r_ff_8 (.S(out_1[7]), .R(not_8_out), .Q(out_2[7]));  // open: clk, Qn, preset, reset, en
endmodule

module CU (
  input  [2:0] in_1,
  output out_2,
  output ramwrite,
  output address,
  output [1:0] ALU_OP
);

  wire and_3_out, and_4_out, and_5_out, and_7_out;

  // AND_Gate and_1 has open pins: in0=in_1[2], in1=in_1[1], in2=in_1[0], out=open
  and and_2 (ramwrite, ~in_1[2], ~in_1[1], in_1[0]);  // AND_Gate
  and and_3 (and_3_out, ~in_1[2], in_1[1], ~in_1[0]);  // AND_Gate
  and and_4 (and_4_out, in_1[2], ~in_1[1], ~in_1[0]);  // AND_Gate
  and and_5 (and_5_out, ~in_1[2], in_1[1], in_1[0]);  // AND_Gate
  and and_6 (ALU_OP[0], in_1[2], in_1[1], ~in_1[0]);  // AND_Gate
  and and_7 (and_7_out, in_1[2], ~in_1[1], in_1[0]);  // AND_Gate
  and and_8 (ALU_OP[1], in_1[2], in_1[1], in_1[0]);
  or or_1 (address, and_3_out, ramwrite);
endmodule

module IR (
  input  [3:0] in_1,
  input  [7:0] instrval,
  output [2:0] OPCODE,
  output argv_0,
  output [3:0] argv_1,
  output [3:0] instrcacheaddr
);


  assign argv_0 = instrval[3];
  assign argv_1 = instrval[7:4];
  assign instrcacheaddr = in_1;
  assign OPCODE = instrval[2:0];
endmodule

module cache (
  input  [7:0] writeval,
  input  status,
  input  [3:0] raddress,
  input  [3:0] waddress,
  output [7:0] out_5
);

  wire and_1_out, and_2_out, and_3_out, and_4_out, and_5_out, and_6_out, and_7_out, and_8_out, and_9_out,
       and_10_out, and_11_out, and_12_out, and_13_out, and_14_out, and_15_out, and_16_out, not_1_out,
       not_2_out, not_3_out, not_4_out, not_5_out, not_6_out, not_7_out, not_8_out, not_9_out, not_10_out,
       not_11_out, not_12_out, not_13_out, not_14_out, not_15_out, not_16_out;
  wire [3:0] multiplexer_1_out;
  wire [7:0] cachebyte_1_read_val, cachebyte_5_read_val, cachebyte_9_read_val, cachebyte_13_read_val;

  Multiplexer #(.width(4)) multiplexer_1 (
    .in0(raddress), .in1(waddress), .out(multiplexer_1_out), .sel(status));  // open: en
  not not_1 (not_1_out, multiplexer_1_out[0]);
  not not_2 (not_2_out, multiplexer_1_out[1]);
  not not_3 (not_3_out, multiplexer_1_out[0]);
  not not_4 (not_4_out, multiplexer_1_out[1]);
  cachebyte cachebyte_1 (.status(status), .address(and_1_out), .write_val(writeval), .read_val(cachebyte_1_read_val));
  and and_1 (and_1_out, not_1_out, not_2_out);
  and and_2 (and_2_out, not_3_out, multiplexer_1_out[1]);
  cachebyte cachebyte_2 (.status(status), .address(and_2_out), .write_val(writeval), .read_val(cachebyte_1_read_val));
  and and_3 (and_3_out, multiplexer_1_out[0], not_4_out);
  cachebyte cachebyte_3 (.status(status), .address(and_3_out), .write_val(writeval), .read_val(cachebyte_1_read_val));
  and and_4 (and_4_out, multiplexer_1_out[0], multiplexer_1_out[1]);
  cachebyte cachebyte_4 (.status(status), .address(and_4_out), .write_val(writeval), .read_val(cachebyte_1_read_val));
  not not_5 (not_5_out, multiplexer_1_out[0]);
  not not_6 (not_6_out, multiplexer_1_out[1]);
  not not_7 (not_7_out, multiplexer_1_out[0]);
  not not_8 (not_8_out, multiplexer_1_out[1]);
  cachebyte cachebyte_5 (.status(status), .address(and_5_out), .write_val(writeval), .read_val(cachebyte_5_read_val));
  and and_5 (and_5_out, not_5_out, not_6_out);
  and and_6 (and_6_out, not_7_out, multiplexer_1_out[1]);
  cachebyte cachebyte_6 (.status(status), .address(and_6_out), .write_val(writeval), .read_val(cachebyte_5_read_val));
  cachebyte cachebyte_7 (.status(status), .address(and_7_out), .write_val(writeval), .read_val(cachebyte_5_read_val));
  and and_7 (and_7_out, multiplexer_1_out[0], not_8_out);
  and and_8 (and_8_out, multiplexer_1_out[0], multiplexer_1_out[1]);
  cachebyte cachebyte_8 (.status(status), .address(and_8_out), .write_val(writeval), .read_val(cachebyte_5_read_val));
  not not_9 (not_9_out, multiplexer_1_out[0]);
  not not_10 (not_10_out, multiplexer_1_out[1]);
  not not_11 (not_11_out, multiplexer_1_out[0]);
  not not_12 (not_12_out, multiplexer_1_out[1]);
  and and_9 (and_9_out, not_9_out, not_10_out);
  and and_10 (and_10_out, not_11_out, multiplexer_1_out[1]);
  and and_11 (and_11_out, multiplexer_1_out[0], not_12_out);
  and and_12 (and_12_out, multiplexer_1_out[0], multiplexer_1_out[1]);
  Multiplexer #(.select(2), .width(8)) multiplexer_2 (
    .in0(cachebyte_1_read_val), .in1(cachebyte_5_read_val), .in2(cachebyte_9_read_val),
    .in3(cachebyte_13_read_val), .out(out_5), .sel({multiplexer_1_out[2], multiplexer_1_out[3]}));  // open: en
  cachebyte cachebyte_9 (.status(status), .address(and_9_out), .write_val(writeval), .read_val(cachebyte_9_read_val));
  cachebyte cachebyte_10 (.status(status), .address(and_10_out), .write_val(writeval), .read_val(cachebyte_9_read_val));
  cachebyte cachebyte_11 (.status(status), .address(and_11_out), .write_val(writeval), .read_val(cachebyte_9_read_val));
  cachebyte cachebyte_12 (.status(status), .address(and_12_out), .write_val(writeval), .read_val(cachebyte_9_read_val));
  not not_13 (not_13_out, multiplexer_1_out[0]);
  and and_13 (and_13_out, not_13_out, not_14_out);
  not not_14 (not_14_out, multiplexer_1_out[1]);
  not not_15 (not_15_out, multiplexer_1_out[0]);
  and and_14 (and_14_out, not_15_out, multiplexer_1_out[1]);
  and and_15 (and_15_out, multiplexer_1_out[0], not_16_out);
  not not_16 (not_16_out, multiplexer_1_out[1]);
  and and_16 (and_16_out, multiplexer_1_out[0], multiplexer_1_out[1]);
  cachebyte cachebyte_13 (
    .status(status), .address(and_13_out), .write_val(writeval), .read_val(cachebyte_13_read_val));
  cachebyte cachebyte_14 (
    .status(status), .address(and_14_out), .write_val(writeval), .read_val(cachebyte_13_read_val));
  cachebyte cachebyte_15 (
    .status(status), .address(and_15_out), .write_val(writeval), .read_val(cachebyte_13_read_val));
  cachebyte cachebyte_16 (
    .status(status), .address(and_16_out), .write_val(writeval), .read_val(cachebyte_13_read_val));
endmodule

module cachebyte (
  input  status,
  input  address,
  input  [7:0] write_val,
  output [7:0] read_val
);

  wire and_1_out;
  wire [7:0] s_r_ff_1_q;

  and and_1 (and_1_out, status, address);
  S_R_Flip_Flop s_r_ff_1 (
    .S(write_val[0]), .clk(address), .R(and_1_out), .Q(s_r_ff_1_q[0]));  // open: Qn, preset, reset, en
  S_R_Flip_Flop s_r_ff_2 (
    .S(write_val[1]), .clk(address), .R(and_1_out), .Q(s_r_ff_1_q[1]));  // open: Qn, preset, reset, en
  S_R_Flip_Flop s_r_ff_3 (
    .S(write_val[2]), .clk(address), .R(and_1_out), .Q(s_r_ff_1_q[2]));  // open: Qn, preset, reset, en
  S_R_Flip_Flop s_r_ff_4 (
    .S(write_val[3]), .clk(address), .R(and_1_out), .Q(s_r_ff_1_q[3]));  // open: Qn, preset, reset, en
  S_R_Flip_Flop s_r_ff_5 (
    .S(write_val[4]), .clk(address), .R(and_1_out), .Q(s_r_ff_1_q[4]));  // open: Qn, preset, reset, en
  S_R_Flip_Flop s_r_ff_6 (
    .S(write_val[5]), .clk(address), .R(and_1_out), .Q(s_r_ff_1_q[5]));  // open: Qn, preset, reset, en
  S_R_Flip_Flop s_r_ff_7 (
    .S(write_val[6]), .clk(address), .R(and_1_out), .Q(s_r_ff_1_q[6]));  // open: Qn, preset, reset, en
  S_R_Flip_Flop s_r_ff_8 (
    .S(write_val[7]), .clk(address), .R(and_1_out), .Q(s_r_ff_1_q[7]));  // open: Qn, preset, reset, en
  assign read_val = address ? s_r_ff_1_q : 8'bz;  // Controlled_Buffer controlled_buffer_1
endmodule

module fetch (
  input  address,
  input  write,
  input  register_x,
  input  [3:0] address_2,
  input  [7:0] X,
  input  [7:0] Y,
  input  [7:0] writeval,
  output [7:0] X_2,
  output [7:0] Y_2,
  output [7:0] val,
  output [1:0] write_2,
  output GP_x,
  output GP_y
);

  wire not_1_out;
  wire [7:0] bit_extender_1_out;

  assign bit_extender_1_out = {{4{1'b0}}, address_2};  // Bit_Extender bit_extender_1
  not not_1 (not_1_out, address);
  Multiplexer #(.width(8)) multiplexer_1 (.in0(bit_extender_1_out), .in1(Y), .out(Y_2), .sel(not_1_out));  // open: en

  assign GP_x = register_x;
  assign GP_y = address_2[0];
  assign val = writeval;
  assign write_2 = {register_x, write};
  assign X_2 = X;
endmodule

module gpregisters (
  input  select0,
  input  select1,
  input  [7:0] writeval,
  input  [1:0] write,
  output [7:0] read0,
  output [7:0] read1
);

  wire [7:0] demultiplexer_1_out0, demultiplexer_1_out1, register_1_out_2, register_2_out_2;

  Demultiplexer #(.width(8)) demultiplexer_1 (
    .out0(demultiplexer_1_out0), .out1(demultiplexer_1_out1), .in(writeval), .sel(write[1]), .en(write[0]));
  register register_1 (.out_1(demultiplexer_1_out0), .out_2(register_1_out_2));
  register register_2 (.out_1(demultiplexer_1_out1), .out_2(register_2_out_2));
  Multiplexer #(.width(8)) multiplexer_1 (
    .in0(register_1_out_2), .in1(register_2_out_2), .out(read0), .sel(select0));  // open: en
  Multiplexer #(.width(8)) multiplexer_2 (
    .in0(register_1_out_2), .in1(register_2_out_2), .out(read1), .sel(select1));  // open: en
endmodule

module store (
  input  ramwrite,
  input  [7:0] value,
  input  [7:0] cache_address,
  input  register_address,
  input  [1:0] register_write,
  output [7:0] value_2,
  output [3:0] cache_address_2,
  output ram_write
);

  not not_1 (register_write[0], ramwrite);

  assign cache_address_2 = cache_address[3:0];
  assign ram_write = ramwrite;
  assign register_write[1] = register_address;
  assign value_2 = value;
endmodule
